# Fritzing sketch Bootloader_layout (saved by Fritzing 0.9.3b)
breadboards: 1

parts:
  Part1 = Arduino Nano (Rev3.0)
  J1 = AVR ISP 6 Pin [package=2x3-ns]
  C1 = Electrolytic Capacitor [capacitance=10nF package="100 mil [THT, electrolytic]"]

nets:
  N1: Part1.GND, J1.6, C1.-
  N2: Part1.D10, J1.5
  N3: Part1.D11/MOSI, J1.4
  N4: Part1.D12/MISO, J1.1
  N5: Part1.RESET, C1.+
  N6: Part1.5V, J1.2
  N7: Part1.D13/SCK, J1.3
